// Logisim project C1_Group1.circ as structural Verilog: 6 circuits, main circuit Circuit without pipelining
// Control unit
module ControlUnit (
  input  [3:0] PC,
  output [2:0] AluOp,
  output AluSrc,
  output bneq,
  output beq,
  output memToReg,
  output memWrite,
  output memRead,
  output RegWrite,
  output RegDst,
  output shift,
  output jump
);

  ROM #(.addrWidth(4), .dataWidth(13)) rom_1 (
    .addr(PC), .data({jump, shift, RegDst, RegWrite, memRead, memWrite, memToReg, beq, bneq, AluSrc, AluOp}));  // open: sel

  // Notes on the sheet:
  //   contents of rom_1 (hex, n*v repeats v):
  //   11 603 602 604 348 20b 88 e0d 600 601 209 1000 20a 208 e0e 21
endmodule

// Data memory
module dataMemory (
  input  [7:0] Address,
  input  [7:0] Data_Input,
  input  isSP,
  input  Store,
  input  Chip_Select,
  input  Clock,
  input  clear,
  input  Load,
  output [7:0] Data_Loaded
);

  wire and_1_out, and_2_out, not_1_out;

  not not_1 (not_1_out, isSP);
  and and_1 (and_1_out, not_1_out, Store);
  and and_2 (and_2_out, not_1_out, Load);
  RAM #(.bus("separate")) ram_1 (
    .addr(Address), .din(Data_Input), .data(Data_Loaded), .str(and_1_out), .sel(Chip_Select), .clk(Clock),
    .ld(and_2_out), .clr(clear));
endmodule

// intruction memory
module Insruction_memory (
  input  [7:0] PC,
  output [19:0] Instruction
);

  ROM #(.dataWidth(20)) rom_1 (.addr(PC), .data(Instruction));  // open: sel

  // Notes on the sheet:
  //   contents of rom_1 (hex, n*v repeats v):
  //   d010a d0201 f1209 d0202 f1209 d0201 d0301 d0502 82340 80320 80430 d5501 51fb b0f00 d0401 67400 a7701
  //   e4014 67100 a7701 71055 67500 a7701 655a2 67500 a7701 452a2 67200 a7701 d2388 67300 a7701 a3481
  //   94340 67400 a7701 d0146 d0255 11230 67300 a7701 534fe 67400 a7701 d0480 d05aa 24520 67200 a7701
  //   c23ff 67300 a7701 b3400
endmodule

// Reg file
module Register_File (
  input  [3:0] Read_Reg1__rs,
  input  [3:0] Read_Reg2__rt,
  input  [3:0] Write_register,
  input  [7:0] Write_Data,
  input  Clock,
  input  Write_signal,
  input  clear,
  output [7:0] Read_data_1,
  output [7:0] Read_data_2,
  output [7:0] zero,
  output [7:0] t0,
  output [7:0] t1,
  output [7:0] t2,
  output [7:0] t3,
  output [7:0] t4,
  output [7:0] t5,
  output [7:0] sp
);

  wire and_1_out, and_2_out, and_3_out, and_4_out, and_5_out, and_6_out, and_7_out, and_8_out,
       decoder_1_out0, decoder_1_out1, decoder_1_out2, decoder_1_out3, decoder_1_out4, decoder_1_out5,
       decoder_1_out6, decoder_1_out7, multiplexer_2_out, multiplexer_3_out;
  wire [7:0] multiplexer_1_out;

  Decoder #(.select(4), .enable("false")) decoder_1 (
    .out0(decoder_1_out0), .out1(decoder_1_out1), .out2(decoder_1_out2), .out3(decoder_1_out3),
    .out4(decoder_1_out4), .out5(decoder_1_out5), .out6(decoder_1_out6), .out7(decoder_1_out7),
    .sel(Write_register));  // open: out8, out9, out10, out11, out12, out13, out14, out15
  and and_1 (and_1_out, decoder_1_out0, 1'b0);
  and and_2 (and_2_out, decoder_1_out1, Write_signal);
  and and_3 (and_3_out, decoder_1_out2, Write_signal);
  and and_4 (and_4_out, decoder_1_out3, Write_signal);
  and and_5 (and_5_out, decoder_1_out4, Write_signal);
  and and_6 (and_6_out, decoder_1_out5, Write_signal);
  and and_7 (and_7_out, decoder_1_out6, Write_signal);
  and and_8 (and_8_out, decoder_1_out7, Write_signal);
  Multiplexer #(.width(8), .enable("false")) multiplexer_1 (
    .in0(Write_Data), .in1({8{1'b1}}), .out(multiplexer_1_out), .sel(clear));
  Register u_zero (.D(Write_Data), .en(and_1_out), .Q(zero), .clk(Clock), .clr(clear));
  Register u_t0 (.D(Write_Data), .en(and_2_out), .Q(t0), .clk(Clock), .clr(clear));
  Register u_t1 (.D(Write_Data), .en(and_3_out), .Q(t1), .clk(Clock), .clr(clear));
  Register u_t2 (.D(Write_Data), .en(and_4_out), .Q(t2), .clk(Clock), .clr(clear));
  Register u_t3 (.D(Write_Data), .en(and_5_out), .Q(t3), .clk(Clock), .clr(clear));
  Register u_t4 (.D(Write_Data), .en(and_6_out), .Q(t4), .clk(Clock), .clr(clear));
  Register u_t5 (.D(Write_Data), .en(and_7_out), .Q(t5), .clk(Clock), .clr(clear));
  Multiplexer #(.enable("false")) multiplexer_2 (.in0(and_8_out), .in1(clear), .out(multiplexer_2_out), .sel(clear));
  Multiplexer #(.enable("false")) multiplexer_3 (.in0(Clock), .in1(clear), .out(multiplexer_3_out), .sel(clear));
  Register u_sp (.D(multiplexer_1_out), .en(multiplexer_2_out), .Q(sp), .clk(multiplexer_3_out));  // open: clr
  Multiplexer #(.select(4), .width(8), .enable("false")) multiplexer_4 (
    .in0(zero), .in1(t0), .in2(t1), .in3(t2), .in4(t3), .in5(t4), .in6(t5), .in7(sp), .out(Read_data_1),
    .sel(Read_Reg1__rs));  // open: in8, in9, in10, in11, in12, in13, in14, in15
  Multiplexer #(.select(4), .width(8), .enable("false")) multiplexer_5 (
    .in0(zero), .in1(t0), .in2(t1), .in3(t2), .in4(t3), .in5(t4), .in6(t5), .in7(sp), .out(Read_data_2),
    .sel(Read_Reg2__rt));  // open: in8, in9, in10, in11, in12, in13, in14, in15
endmodule

module Circuit_without_pipelining (
  input  clear,
  output [3:0] opcode,
  output [7:0] PC,
  output [19:0] Instr_adr,
  output [7:0] alu_out,
  output [7:0] read_data_2,
  output [7:0] B,
  output [3:0] rt,
  output [7:0] read_data_1,
  output [7:0] dm_out,
  output [3:0] rs,
  output [3:0] rd,
  output [3:0] fin_rd,
  output [3:0] shmt,
  output [7:0] B_2,
  output [7:0] zero_reg,
  output [7:0] t0,
  output [7:0] t1,
  output [7:0] t2,
  output [7:0] t3,
  output [7:0] t4,
  output [7:0] t5,
  output [7:0] sp,
  output [7:0] write_data
);

  wire alu_8_by_art_1_p4, and_1_out, and_2_out, and_3_out, clock_out, controlunit_1_alusrc,
       controlunit_1_beq, controlunit_1_bneq, controlunit_1_jump, controlunit_1_memread,
       controlunit_1_memtoreg, controlunit_1_memwrite, controlunit_1_regdst, controlunit_1_regwrite,
       controlunit_1_shift, not_1_out, not_2_out;
  wire [1:0] priority_encoder_1_out;
  wire [2:0] controlunit_1_aluop;
  wire [7:0] adder_1_out, adder_2_out, multiplexer_4_out, multiplexer_5_out, multiplexer_7_out,
       multiplexer_8_out, stackmemory_1_data_loaded;

  Clock clock (.out(clock_out));
  Adder adder_1 (.a(PC), .b(8'h1), .out(adder_1_out), .cin(1'b0));  // open: cout
  Register #(.trigger("falling")) PC_reg (.D(multiplexer_8_out), .Q(PC), .clk(clock_out), .clr(clear));  // open: en
  Insruction_memory insruction_memory_1 (.PC(PC), .Instruction({Instr_adr[19:4], B_2[3:0]}));
  ControlUnit controlunit_1 (
    .PC(Instr_adr[19:16]), .AluOp(controlunit_1_aluop), .AluSrc(controlunit_1_alusrc),
    .bneq(controlunit_1_bneq), .beq(controlunit_1_beq), .memToReg(controlunit_1_memtoreg),
    .memWrite(controlunit_1_memwrite), .memRead(controlunit_1_memread), .RegWrite(controlunit_1_regwrite),
    .RegDst(controlunit_1_regdst), .shift(controlunit_1_shift), .jump(controlunit_1_jump));
  Multiplexer #(.width(4), .enable("false")) multiplexer_1 (
    .in0(Instr_adr[7:4]), .in1(4'b0000), .out(B_2[7:4]), .sel(controlunit_1_shift));
  Multiplexer #(.width(4), .enable("false")) multiplexer_2 (
    .in0(Instr_adr[11:8]), .in1(Instr_adr[7:4]), .out(fin_rd), .sel(controlunit_1_regdst));
  Adder adder_2 (.a(adder_1_out), .b(B_2), .out(adder_2_out), .cin(1'b0));  // open: cout
  Register_File register_file_1 (
    .Read_Reg1__rs(Instr_adr[15:12]), .Read_Reg2__rt(Instr_adr[11:8]), .Write_register(fin_rd),
    .Write_Data(write_data), .Write_signal(controlunit_1_regwrite), .Clock(clock_out), .clear(clear),
    .Read_data_1(read_data_1), .Read_data_2(read_data_2), .zero(zero_reg), .t0(t0), .t1(t1), .t2(t2),
    .t3(t3), .t4(t4), .t5(t5), .sp(sp));
  Multiplexer #(.width(8), .enable("false")) multiplexer_3 (
    .in0(read_data_2), .in1(B_2), .out(B), .sel(controlunit_1_alusrc));
  Multiplexer #(.width(8), .enable("false")) multiplexer_4 (
    .in0(read_data_1), .in1(B), .out(multiplexer_4_out), .sel(controlunit_1_shift));
  Multiplexer #(.width(8), .enable("false")) multiplexer_5 (
    .in0(B), .in1(read_data_1), .out(multiplexer_5_out), .sel(controlunit_1_shift));
  // ALU_8_by_ART alu_8_by_art_1: pin names not known; wires that end beside it: multiplexer_4_out, multiplexer_5_out, controlunit_1_aluop, alu_8_by_art_1_p4, alu_out
  not not_1 (not_1_out, Instr_adr[15]);
  and and_1 (and_1_out, Instr_adr[12], Instr_adr[13], Instr_adr[14], not_1_out);
  not not_2 (not_2_out, alu_8_by_art_1_p4);
  and and_2 (and_2_out, controlunit_1_bneq, not_2_out);
  and and_3 (and_3_out, controlunit_1_beq, alu_8_by_art_1_p4);
  dataMemory datamemory_1 (
    .Address(alu_out), .Data_Input(read_data_2), .isSP(and_1_out), .Store(controlunit_1_memwrite),
    .Clock(clock_out), .Load(controlunit_1_memread), .clear(clear), .Data_Loaded(dm_out));  // open: Chip_Select
  stackmemory stackmemory_1 (
    .Address(alu_out), .Data_Input(read_data_2), .sp(and_1_out), .Store(controlunit_1_memwrite),
    .Clock(clock_out), .Load(controlunit_1_memread), .Clear(clear), .Data_Loaded(stackmemory_1_data_loaded));  // open: Chip_Select
  Multiplexer #(.width(8), .enable("false")) multiplexer_6 (
    .in0(alu_out), .in1(multiplexer_7_out), .out(write_data), .sel(controlunit_1_memtoreg));
  Multiplexer #(.width(8), .enable("false")) multiplexer_7 (
    .in0(dm_out), .in1(stackmemory_1_data_loaded), .out(multiplexer_7_out), .sel(and_1_out));
  Priority_Encoder #(.select(2)) priority_encoder_1 (
    .in0(1'b1), .in1(and_2_out), .in2(and_3_out), .in3(controlunit_1_jump), .out(priority_encoder_1_out));  // open: gs, en_out, en_in
  Multiplexer #(.select(2), .width(8), .enable("false")) multiplexer_8 (
    .in0(adder_1_out), .in1(adder_2_out), .in2(adder_2_out), .in3(Instr_adr[15:8]), .out(multiplexer_8_out),
    .sel(priority_encoder_1_out));

  assign Instr_adr[3:0] = B_2[3:0];
  assign opcode = Instr_adr[19:16];
  assign rd = Instr_adr[7:4];
  assign rs = Instr_adr[15:12];
  assign rt = Instr_adr[11:8];
  assign shmt = B_2[3:0];
endmodule

// stack mem
module stackmemory (
  input  [7:0] Address,
  input  [7:0] Data_Input,
  input  Clear,
  input  sp,
  input  Store,
  input  Clock,
  input  Load,
  input  Chip_Select,
  output [7:0] Data_Loaded
);

  wire and_1_out, and_2_out;

  and and_1 (and_1_out, sp, Store);
  and and_2 (and_2_out, sp, Load);
  RAM #(.bus("separate")) ram_1 (
    .addr(Address), .din(Data_Input), .data(Data_Loaded), .str(and_1_out), .sel(Chip_Select), .clk(Clock),
    .ld(and_2_out), .clr(Clear));
endmodule
