// Logisim project C1_Group1_PIP.circ as structural Verilog: 14 circuits, main circuit Circuit Pipelining
// Control unit
module ControlUnit (
  input  [3:0] PC,
  output [2:0] AluOp,
  output AluSrc,
  output bneq,
  output beq,
  output memToReg,
  output memWrite,
  output memRead,
  output RegWrite,
  output RegDst,
  output shift,
  output jump
);

  ROM #(.addrWidth(4), .dataWidth(13)) rom_1 (
    .addr(PC), .data({jump, shift, RegDst, RegWrite, memRead, memWrite, memToReg, beq, bneq, AluSrc, AluOp}));  // open: sel

  // Notes on the sheet:
  //   contents of rom_1 (hex, n*v repeats v):
  //   11 603 602 604 348 20b 88 e0d 600 601 209 1000 20a 208 e0e 21
endmodule

// Data memory
module dataMemory (
  input  [7:0] Address,
  input  [7:0] Data_Input,
  input  isSP,
  input  Store,
  input  Chip_Select,
  input  Clock,
  input  clear,
  input  Load,
  output [7:0] Data_Loaded
);

  wire and_1_out, and_2_out, not_1_out;

  not not_1 (not_1_out, isSP);
  and and_1 (and_1_out, not_1_out, Store);
  and and_2 (and_2_out, not_1_out, Load);
  RAM #(.bus("separate")) ram_1 (
    .addr(Address), .din(Data_Input), .data(Data_Loaded), .str(and_1_out), .sel(Chip_Select), .clk(Clock),
    .ld(and_2_out), .clr(clear));
endmodule

// intruction memory
module Insruction_memory (
  input  [7:0] PC,
  output [19:0] Instruction
);

  ROM #(.dataWidth(20)) rom_1 (.addr(PC), .data(Instruction));  // open: sel

  // Notes on the sheet:
  //   contents of rom_1 (hex, n*v repeats v):
  //   d010a d0201 f1209 d0202 f1209 d0201 d0301 d0502 82340 80320 80430 d5501 51fb b0f00 d0401 67400 a7701
  //   e4014 67100 a7701 71055 67500 a7701 655a2 67500 a7701 452a2 67200 a7701 d2388 67300 a7701 a3481
  //   94340 67400 a7701 d0146 d0255 11230 67300 a7701 534fe 67400 a7701 d0480 d05aa 24520 67200 a7701
  //   c23ff 67300 a7701 b3400
endmodule

// Reg file
module Register_File (
  input  [3:0] Read_Reg1__rs,
  input  [3:0] Read_Reg2__rt,
  input  [3:0] Write_register,
  input  [7:0] Write_Data,
  input  Clock,
  input  Write_signal,
  input  clear,
  output [7:0] Read_data_1,
  output [7:0] Read_data_2,
  output [7:0] zero,
  output [7:0] t0,
  output [7:0] t1,
  output [7:0] t2,
  output [7:0] t3,
  output [7:0] t4,
  output [7:0] t5,
  output [7:0] sp
);

  wire and_1_out, and_2_out, and_3_out, and_4_out, and_5_out, and_6_out, and_7_out, and_8_out,
       decoder_1_out0, decoder_1_out1, decoder_1_out2, decoder_1_out3, decoder_1_out4, decoder_1_out5,
       decoder_1_out6, decoder_1_out7, multiplexer_2_out, multiplexer_3_out;
  wire [7:0] multiplexer_1_out;

  Decoder #(.select(4), .enable("false")) decoder_1 (
    .out0(decoder_1_out0), .out1(decoder_1_out1), .out2(decoder_1_out2), .out3(decoder_1_out3),
    .out4(decoder_1_out4), .out5(decoder_1_out5), .out6(decoder_1_out6), .out7(decoder_1_out7),
    .sel(Write_register));  // open: out8, out9, out10, out11, out12, out13, out14, out15
  and and_1 (and_1_out, decoder_1_out0, 1'b0);
  and and_2 (and_2_out, decoder_1_out1, Write_signal);
  and and_3 (and_3_out, decoder_1_out2, Write_signal);
  and and_4 (and_4_out, decoder_1_out3, Write_signal);
  and and_5 (and_5_out, decoder_1_out4, Write_signal);
  and and_6 (and_6_out, decoder_1_out5, Write_signal);
  and and_7 (and_7_out, decoder_1_out6, Write_signal);
  and and_8 (and_8_out, decoder_1_out7, Write_signal);
  Multiplexer #(.width(8), .enable("false")) multiplexer_1 (
    .in0(Write_Data), .in1({8{1'b1}}), .out(multiplexer_1_out), .sel(clear));
  Register u_zero (.D(Write_Data), .en(and_1_out), .Q(zero), .clk(Clock), .clr(clear));
  Register u_t0 (.D(Write_Data), .en(and_2_out), .Q(t0), .clk(Clock), .clr(clear));
  Register u_t1 (.D(Write_Data), .en(and_3_out), .Q(t1), .clk(Clock), .clr(clear));
  Register u_t2 (.D(Write_Data), .en(and_4_out), .Q(t2), .clk(Clock), .clr(clear));
  Register u_t3 (.D(Write_Data), .en(and_5_out), .Q(t3), .clk(Clock), .clr(clear));
  Register u_t4 (.D(Write_Data), .en(and_6_out), .Q(t4), .clk(Clock), .clr(clear));
  Register u_t5 (.D(Write_Data), .en(and_7_out), .Q(t5), .clk(Clock), .clr(clear));
  Multiplexer #(.enable("false")) multiplexer_2 (.in0(and_8_out), .in1(clear), .out(multiplexer_2_out), .sel(clear));
  Multiplexer #(.enable("false")) multiplexer_3 (.in0(Clock), .in1(clear), .out(multiplexer_3_out), .sel(clear));
  Register u_sp (.D(multiplexer_1_out), .en(multiplexer_2_out), .Q(sp), .clk(multiplexer_3_out));  // open: clr
  Multiplexer #(.select(4), .width(8), .enable("false")) multiplexer_4 (
    .in0(zero), .in1(t0), .in2(t1), .in3(t2), .in4(t3), .in5(t4), .in6(t5), .in7(sp), .out(Read_data_1),
    .sel(Read_Reg1__rs));  // open: in8, in9, in10, in11, in12, in13, in14, in15
  Multiplexer #(.select(4), .width(8), .enable("false")) multiplexer_5 (
    .in0(zero), .in1(t0), .in2(t1), .in3(t2), .in4(t3), .in5(t4), .in6(t5), .in7(sp), .out(Read_data_2),
    .sel(Read_Reg2__rt));  // open: in8, in9, in10, in11, in12, in13, in14, in15
endmodule

// fwd unit
module Forwarding_Unit (
  input  [3:0] EX_MEM_rd,
  input  [3:0] ID_EX_rs,
  input  [3:0] ID_EX_rt,
  input  [3:0] MEM_WB_rd,
  input  regwrite,
  output [1:0] Forward_A,
  output [1:0] Forward_B
);

  wire and_1_out, and_6_out, nor_1_out, nor_2_out, nor_3_out, nor_4_out, or_1_out, or_2_out;
  wire [3:0] and_5_out, subtractor_1_out, subtractor_2_out, subtractor_3_out, subtractor_4_out;

  or or_1 (or_1_out, EX_MEM_rd[0], EX_MEM_rd[1], EX_MEM_rd[2], EX_MEM_rd[3]);
  Subtractor #(.width(4)) subtractor_1 (.a(EX_MEM_rd), .b(ID_EX_rs), .out(subtractor_1_out), .bin(1'b0));  // open: bout
  Subtractor #(.width(4)) subtractor_2 (.a(EX_MEM_rd), .b(ID_EX_rt), .out(subtractor_2_out), .bin(1'b0));  // open: bout
  or or_2 (or_2_out, MEM_WB_rd[0], MEM_WB_rd[1], MEM_WB_rd[2], MEM_WB_rd[3]);
  Subtractor #(.width(4)) subtractor_3 (.a(MEM_WB_rd), .b(ID_EX_rs), .out(subtractor_3_out), .bin(1'b0));  // open: bout
  Subtractor #(.width(4)) subtractor_4 (.a(MEM_WB_rd), .b(ID_EX_rt), .out(subtractor_4_out), .bin(1'b0));  // open: bout
  nor nor_1 (nor_1_out, subtractor_1_out[0], subtractor_1_out[1], subtractor_1_out[2], subtractor_1_out[3]);
  nor nor_2 (nor_2_out, subtractor_2_out[0], subtractor_2_out[1], subtractor_2_out[2], subtractor_2_out[3]);
  nor nor_3 (nor_3_out, subtractor_3_out[0], subtractor_3_out[1], subtractor_3_out[2], subtractor_3_out[3]);
  nor nor_4 (nor_4_out, subtractor_4_out[0], subtractor_4_out[1], subtractor_4_out[2], subtractor_4_out[3]);
  and and_1 (and_1_out, regwrite, or_1_out);
  and and_2 (and_5_out[3], and_1_out, nor_1_out);
  and and_3 (and_5_out[2], and_1_out, nor_2_out);
  and and_4 (and_5_out[1], nor_3_out, and_6_out);
  and and_5 (and_5_out[0], nor_4_out, and_6_out);
  and and_6 (and_6_out, or_2_out, regwrite);
  ROM #(.addrWidth(4), .dataWidth(4)) rom_1 (.addr(and_5_out), .data({Forward_A, Forward_B}), .sel(1'b1));

  // Notes on the sheet:
  //   all not zero then we get 1
  //   all not zero then we get 1
  //   contents of rom_1 (hex, n*v repeats v):
  //   0 1 4 5 2 2 6 6 8 9 8 9 4*a
endmodule

// ckt pipeline
module Circuit_Pipelining (
  input  clear,
  output [7:0] alures,
  output [7:0] alures_2,
  output [7:0] read_data_from_mem,
  output [7:0] from_dm,
  output [7:0] PC,
  output [7:0] alures_3,
  output [3:0] rs,
  output [7:0] data,
  output [3:0] rt,
  output [3:0] rd,
  output [7:0] alures_4,
  output [7:0] alures_5,
  output [3:0] shamt,
  output [7:0] A,
  output [7:0] B,
  output [7:0] alures_6,
  output [7:0] write_data,
  output [1:0] forward_A,
  output [3:0] write_reg,
  output [1:0] forward_B,
  output [7:0] zero,
  output [7:0] t0,
  output [7:0] t1,
  output [7:0] t2,
  output [7:0] t3,
  output [7:0] t4,
  output [7:0] t5,
  output [7:0] sp
);

  wire alu_8_by_art_1_p4, and_1_out, and_2_out, and_3_out, clock_out, controlunit_1_alusrc,
       controlunit_1_beq, controlunit_1_bneq, controlunit_1_jump, controlunit_1_memread,
       controlunit_1_memtoreg, controlunit_1_memwrite, controlunit_1_regdst, controlunit_1_regwrite,
       controlunit_1_shift, ex_mem_1_beq_2, ex_mem_1_bneq_2, ex_mem_1_issp_2, ex_mem_1_memread_2,
       ex_mem_1_memtoreg_2, ex_mem_1_memwrite_2, ex_mem_1_regwrite_2, ex_mem_1_zero_2, id_ex_1_alusrc_2,
       id_ex_1_beq_2, id_ex_1_bneq_2, id_ex_1_issp_2, id_ex_1_memread_2, id_ex_1_memtoreg_2,
       id_ex_1_memwrite_2, id_ex_1_regdst_2, id_ex_1_regwrite_2, id_ex_1_shift_2, mem_wb_1_memtoreg_2,
       mem_wb_1_regwrite_2, not_1_out, not_2_out;
  wire [1:0] priority_encoder_1_out;
  wire [2:0] controlunit_1_aluop, id_ex_1_auop;
  wire [3:0] ex_mem_1_write_register_2, id_ex_1_rd_2, id_ex_1_rs_2, id_ex_1_rt_2, multiplexer_5_out;
  wire [7:0] adder_1_out, adder_2_out, datamemory_1_data_loaded, ex_mem_1_pc_4_2, ex_mem_1_pc_4_shift_2,
       id_ex_1_pc_4_2, id_ex_1_read_data_1_2, id_ex_1_read_data_2_2, id_ex_1_signed_extended, if_id_1_pc_4_2,
       multiplexer_1_out, multiplexer_3_out, multiplexer_4_out, multiplexer_6_out,
       register_file_1_read_data_1, register_file_1_read_data_2, stackmemory_1_data_loaded;
  wire [19:0] insruction_memory_1_instruction;
  wire [19:16] if_id_1_instruction_2;

  Priority_Encoder #(.select(2)) priority_encoder_1 (
    .in0(1'b1), .in1(and_2_out), .in2(and_3_out), .in3(controlunit_1_jump), .out(priority_encoder_1_out));  // open: gs, en_out, en_in
  Multiplexer #(.select(2), .width(8), .enable("false")) multiplexer_1 (
    .in0(adder_1_out), .in1(ex_mem_1_pc_4_shift_2), .in2(ex_mem_1_pc_4_shift_2), .in3({rs, rd}),
    .out(multiplexer_1_out), .sel(priority_encoder_1_out));
  Clock clock (.out(clock_out));
  Register #(.trigger("falling")) PC_reg (.D(multiplexer_1_out), .Q(PC), .clk(clock_out), .clr(clear));  // open: en
  Adder adder_1 (.a(PC), .b(8'h1), .out(adder_1_out));  // open: cin, cout
  Insruction_memory insruction_memory_1 (.PC(PC), .Instruction(insruction_memory_1_instruction));
  IF_ID if_id_1 (
    .pc_4(adder_1_out), .Instruction(insruction_memory_1_instruction), .Clock(clock_out), .Clear(clear),
    .pc_4_2(if_id_1_pc_4_2), .Instruction_2({if_id_1_instruction_2, rs, rd, shamt, alures_6[3:0]}));
  ControlUnit controlunit_1 (
    .PC(if_id_1_instruction_2), .AluOp(controlunit_1_aluop), .AluSrc(controlunit_1_alusrc),
    .bneq(controlunit_1_bneq), .beq(controlunit_1_beq), .memToReg(controlunit_1_memtoreg),
    .memWrite(controlunit_1_memwrite), .memRead(controlunit_1_memread), .RegWrite(controlunit_1_regwrite),
    .RegDst(controlunit_1_regdst), .shift(controlunit_1_shift), .jump(controlunit_1_jump));
  Multiplexer #(.width(4), .enable("false")) multiplexer_2 (
    .in0(shamt), .in1(4'b0000), .out(alures_6[7:4]), .sel(controlunit_1_shift));
  not not_1 (not_1_out, rs[3]);
  and and_1 (and_1_out, rs[0], rs[1], rs[2], not_1_out);
  Register_File register_file_1 (
    .Read_Reg1__rs(rs), .Read_Reg2__rt(rd), .Write_register(write_reg), .Write_Data(alures_4),
    .Write_signal(mem_wb_1_regwrite_2), .Clock(clock_out), .clear(clear),
    .Read_data_1(register_file_1_read_data_1), .Read_data_2(register_file_1_read_data_2), .zero(zero),
    .t0(t0), .t1(t1), .t2(t2), .t3(t3), .t4(t4), .t5(t5), .sp(sp));
  ID_EX id_ex_1 (
    .isSP(and_1_out), .regwrite(controlunit_1_regwrite), .memtoreg(controlunit_1_memtoreg),
    .beq(controlunit_1_beq), .bneq(controlunit_1_bneq), .memread(controlunit_1_memread),
    .memwrite(controlunit_1_memwrite), .regdst(controlunit_1_regdst), .Aluop(controlunit_1_aluop),
    .Alusrc(controlunit_1_alusrc), .pc_4(if_id_1_pc_4_2), .Read_data_1(register_file_1_read_data_1),
    .Read_data_2(register_file_1_read_data_2), .sign_extended(alures_6), .rt(rd), .rd(shamt), .rs(rs),
    .shift(controlunit_1_shift), .clock(clock_out), .clear(clear), .isSp_2(id_ex_1_issp_2),
    .regwrite_2(id_ex_1_regwrite_2), .memtoreg_2(id_ex_1_memtoreg_2), .beq_2(id_ex_1_beq_2),
    .bneq_2(id_ex_1_bneq_2), .memread_2(id_ex_1_memread_2), .memwrite_2(id_ex_1_memwrite_2),
    .regdst_2(id_ex_1_regdst_2), .Auop(id_ex_1_auop), .alusrc_2(id_ex_1_alusrc_2), .pc_4_2(id_ex_1_pc_4_2),
    .read_data_1_2(id_ex_1_read_data_1_2), .read_data_2_2(id_ex_1_read_data_2_2),
    .signed_extended(id_ex_1_signed_extended), .rt_2(id_ex_1_rt_2), .rd_2(id_ex_1_rd_2), .rs_2(id_ex_1_rs_2),
    .shift_2(id_ex_1_shift_2));
  Multiplexer #(.width(8), .enable("false")) multiplexer_3 (
    .in0(id_ex_1_read_data_1_2), .in1(multiplexer_6_out), .out(multiplexer_3_out), .sel(id_ex_1_shift_2));
  Multiplexer #(.width(8), .enable("false")) multiplexer_4 (
    .in0(multiplexer_6_out), .in1(id_ex_1_read_data_1_2), .out(multiplexer_4_out), .sel(id_ex_1_shift_2));
  Multiplexer #(.width(4), .enable("false")) multiplexer_5 (
    .in0(id_ex_1_rt_2), .in1(id_ex_1_rd_2), .out(multiplexer_5_out), .sel(id_ex_1_regdst_2));
  Adder adder_2 (.a(id_ex_1_pc_4_2), .b(id_ex_1_signed_extended), .out(adder_2_out), .cin(1'b0));  // open: cout
  Multiplexer #(.width(8), .enable("false")) multiplexer_6 (
    .in0(id_ex_1_read_data_2_2), .in1(id_ex_1_signed_extended), .out(multiplexer_6_out),
    .sel(id_ex_1_alusrc_2));
  Multiplexer #(.select(2), .width(8), .enable("false")) multiplexer_7 (
    .in0(multiplexer_3_out), .in1(alures_4), .in2(alures), .out(A), .sel(forward_A));  // open: in3
  Forwarding_Unit forwarding_unit_1 (
    .EX_MEM_rd(ex_mem_1_write_register_2), .ID_EX_rs(id_ex_1_rs_2), .ID_EX_rt(id_ex_1_rt_2),
    .MEM_WB_rd(write_reg), .regwrite(mem_wb_1_regwrite_2), .Forward_A(forward_A), .Forward_B(forward_B));
  // ALU_8_by_ART alu_8_by_art_1: pin names not known; wires that end beside it: A, B, id_ex_1_auop, alu_8_by_art_1_p4, alures_5
  Multiplexer #(.select(2), .width(8), .enable("false")) multiplexer_8 (
    .in0(multiplexer_4_out), .in1(alures_4), .in2(alures), .out(B), .sel(forward_B));  // open: in3
  EX_MEM ex_mem_1 (
    .isSP(id_ex_1_issp_2), .regwrite(id_ex_1_regwrite_2), .memtoreg(id_ex_1_memtoreg_2), .beq(id_ex_1_beq_2),
    .bneq(id_ex_1_bneq_2), .memread(id_ex_1_memread_2), .memwrite(id_ex_1_memwrite_2),
    .pc_4_shift(adder_2_out), .pc_4(id_ex_1_pc_4_2), .zero(alu_8_by_art_1_p4), .alu_result(alures_5),
    .read_data_2(id_ex_1_read_data_2_2), .write_register(multiplexer_5_out), .clock(clock_out),
    .clear(clear), .isSp_2(ex_mem_1_issp_2), .regwrite_2(ex_mem_1_regwrite_2),
    .memtoreg_2(ex_mem_1_memtoreg_2), .beq_2(ex_mem_1_beq_2), .bneq_2(ex_mem_1_bneq_2),
    .memread_2(ex_mem_1_memread_2), .memwrite_2(ex_mem_1_memwrite_2), .pc_4_shift_2(ex_mem_1_pc_4_shift_2),
    .pc_4_2(ex_mem_1_pc_4_2), .zero_2(ex_mem_1_zero_2), .alureslut(alures), .read_data_2_2(data),
    .write_register_2(ex_mem_1_write_register_2));
  not not_2 (not_2_out, ex_mem_1_zero_2);
  and and_2 (and_2_out, ex_mem_1_bneq_2, not_2_out);
  and and_3 (and_3_out, ex_mem_1_beq_2, ex_mem_1_zero_2);
  dataMemory datamemory_1 (
    .Address(alures), .Data_Input(data), .isSP(ex_mem_1_issp_2), .Store(ex_mem_1_memwrite_2),
    .Clock(clock_out), .Load(ex_mem_1_memread_2), .clear(clear), .Data_Loaded(datamemory_1_data_loaded));  // open: Chip_Select
  stackmemory stackmemory_1 (
    .Address(alures), .Data_Input(data), .sp(ex_mem_1_issp_2), .Store(ex_mem_1_memwrite_2),
    .Clock(clock_out), .Load(ex_mem_1_memread_2), .Clear(clear), .Data_Loaded(stackmemory_1_data_loaded));  // open: Chip_Select
  MEM_WB mem_wb_1 (
    .regwrite(ex_mem_1_regwrite_2), .memtoreg(ex_mem_1_memtoreg_2), .read_data(read_data_from_mem),
    .aluresult(alures), .write_register(ex_mem_1_write_register_2), .clock(clock_out), .clear(clear),
    .regwrite_2(mem_wb_1_regwrite_2), .memtoreg_2(mem_wb_1_memtoreg_2), .read_data_2(from_dm),
    .aluresukt(alures_2), .write_register_2(write_reg));
  Multiplexer #(.width(8), .enable("false")) multiplexer_9 (
    .in0(datamemory_1_data_loaded), .in1(stackmemory_1_data_loaded), .out(read_data_from_mem),
    .sel(ex_mem_1_issp_2));
  Multiplexer #(.width(8), .enable("false")) multiplexer_10 (
    .in0(alures_2), .in1(from_dm), .out(alures_4), .sel(mem_wb_1_memtoreg_2));

  assign alures_3 = alures;
  assign rt = rd;
  assign write_data = alures_4;
endmodule

module IF_ID (
  input  [7:0] pc_4,
  input  [19:0] Instruction,
  input  Clock,
  input  Clear,
  output [7:0] pc_4_2,
  output [19:0] Instruction_2
);

  Register PC__4 (.D(pc_4), .en(1'b1), .Q(pc_4_2), .clk(Clock), .clr(Clear));
  Register #(.width(20)) u_Instruction (.D(Instruction), .en(1'b1), .Q(Instruction_2), .clk(Clock), .clr(Clear));
endmodule

// Ex
module EX (
  input  Regdst,
  input  [2:0] AluOp,
  input  Alusrc,
  input  clock,
  input  clear,
  output RegDst_2,
  output [2:0] AluOp_2,
  output Alusrc_2
);

  Register #(.width(1)) u_RegDst (.D(Regdst), .en(1'b1), .Q(RegDst_2), .clk(clock), .clr(clear));
  Register #(.width(3)) u_AluOp (.D(AluOp), .en(1'b1), .Q(AluOp_2), .clk(clock), .clr(clear));
  Register #(.width(1)) u_AluSrc (.D(Alusrc), .en(1'b1), .Q(Alusrc_2), .clk(clock), .clr(clear));
endmodule

module M (
  input  beq,
  input  bneq,
  input  MemRead,
  input  MemWrite,
  input  Clock,
  input  Clear,
  output beq_2,
  output bneq_2,
  output MemRead_2,
  output MemWrite_2
);

  Register #(.width(1)) u_beq (.D(beq), .en(1'b1), .Q(beq_2), .clk(Clock), .clr(Clear));
  Register #(.width(1)) u_bneq (.D(bneq), .en(1'b1), .Q(bneq_2), .clk(Clock), .clr(Clear));
  Register #(.width(1)) u_MemRead (.D(MemRead), .en(1'b1), .Q(MemRead_2), .clk(Clock), .clr(Clear));
  Register #(.width(1)) u_MemWrite (.D(MemWrite), .en(1'b1), .Q(MemWrite_2), .clk(Clock), .clr(Clear));
endmodule

module WB (
  input  RegWrite,
  input  MemToReg,
  input  Clock,
  input  Clear,
  output RegWrite_2,
  output MemToReg_2
);

  Register #(.width(1)) u_RegWrite (.D(RegWrite), .en(1'b1), .Q(RegWrite_2), .clk(Clock), .clr(Clear));
  Register #(.width(1)) u_MemToReg (.D(MemToReg), .en(1'b1), .Q(MemToReg_2), .clk(Clock), .clr(Clear));
endmodule

module ID_EX (
  input  isSP,
  input  regwrite,
  input  memtoreg,
  input  beq,
  input  bneq,
  input  memread,
  input  memwrite,
  input  regdst,
  input  [2:0] Aluop,
  input  Alusrc,
  input  [7:0] pc_4,
  input  [7:0] Read_data_1,
  input  [7:0] Read_data_2,
  input  [7:0] sign_extended,
  input  [3:0] rt,
  input  [3:0] rd,
  input  [3:0] rs,
  input  shift,
  input  clock,
  input  clear,
  output isSp_2,
  output regwrite_2,
  output memtoreg_2,
  output beq_2,
  output bneq_2,
  output memread_2,
  output memwrite_2,
  output regdst_2,
  output [2:0] Auop,
  output alusrc_2,
  output [7:0] pc_4_2,
  output [7:0] read_data_1_2,
  output [7:0] read_data_2_2,
  output [7:0] signed_extended,
  output [3:0] rt_2,
  output [3:0] rd_2,
  output [3:0] rs_2,
  output shift_2
);

  Register #(.width(4)) u_rs (.D(rs), .en(1'b1), .Q(rs_2), .clk(clock), .clr(clear));
  Register #(.width(1)) u_shift (.D(shift), .en(1'b1), .Q(shift_2), .clk(clock), .clr(clear));
  Register #(.width(1)) u_issp (.D(isSP), .en(1'b1), .Q(isSp_2), .clk(clock), .clr(clear));
  WB wb_1 (
    .RegWrite(regwrite), .MemToReg(memtoreg), .Clock(clock), .Clear(clear), .RegWrite_2(regwrite_2),
    .MemToReg_2(memtoreg_2));
  M m_1 (
    .beq(beq), .bneq(bneq), .MemRead(memread), .MemWrite(memwrite), .Clock(clock), .Clear(clear),
    .beq_2(beq_2), .bneq_2(bneq_2), .MemRead_2(memread_2), .MemWrite_2(memwrite_2));
  EX ex_1 (
    .Regdst(regdst), .AluOp(Aluop), .Alusrc(Alusrc), .clock(clock), .clear(clear), .RegDst_2(regdst_2),
    .AluOp_2(Auop), .Alusrc_2(alusrc_2));
  Register PC__4 (.D(pc_4), .en(1'b1), .Q(pc_4_2), .clk(clock), .clr(clear));
  Register u_Read_data_1 (.D(Read_data_1), .en(1'b1), .Q(read_data_1_2), .clk(clock), .clr(clear));
  Register u_Read_data_2 (.D(Read_data_2), .en(1'b1), .Q(read_data_2_2), .clk(clock), .clr(clear));
  Register u_sign_extended (.D(sign_extended), .en(1'b1), .Q(signed_extended), .clk(clock), .clr(clear));
  Register #(.width(4)) u_rt (.D(rt), .en(1'b1), .Q(rt_2), .clk(clock), .clr(clear));
  Register #(.width(4)) u_rd (.D(rd), .en(1'b1), .Q(rd_2), .clk(clock), .clr(clear));
endmodule

module EX_MEM (
  input  isSP,
  input  regwrite,
  input  memtoreg,
  input  beq,
  input  bneq,
  input  memread,
  input  memwrite,
  input  [7:0] pc_4_shift,
  input  [7:0] pc_4,
  input  zero,
  input  [7:0] alu_result,
  input  [7:0] read_data_2,
  input  [3:0] write_register,
  input  clock,
  input  clear,
  output isSp_2,
  output regwrite_2,
  output memtoreg_2,
  output beq_2,
  output bneq_2,
  output memread_2,
  output memwrite_2,
  output [7:0] pc_4_shift_2,
  output [7:0] pc_4_2,
  output zero_2,
  output [7:0] alureslut,
  output [7:0] read_data_2_2,
  output [3:0] write_register_2
);

  Register #(.width(1)) u_issp (.D(isSP), .en(1'b1), .Q(isSp_2), .clk(clock), .clr(clear));
  WB wb_1 (
    .RegWrite(regwrite), .MemToReg(memtoreg), .Clock(clock), .Clear(clear), .RegWrite_2(regwrite_2),
    .MemToReg_2(memtoreg_2));
  M m_1 (
    .beq(beq), .bneq(bneq), .MemRead(memread), .MemWrite(memwrite), .Clock(clock), .Clear(clear),
    .beq_2(beq_2), .bneq_2(bneq_2), .MemRead_2(memread_2), .MemWrite_2(memwrite_2));
  Register u_pc_4_shift (.D(pc_4_shift), .en(1'b1), .Q(pc_4_shift_2), .clk(clock), .clr(clear));
  Register u_pc_4 (.D(pc_4), .en(1'b1), .Q(pc_4_2), .clk(clock), .clr(clear));
  Register #(.width(1)) u_zero (.D(zero), .en(1'b1), .Q(zero_2), .clk(clock), .clr(clear));
  Register aluresult (.D(alu_result), .en(1'b1), .Q(alureslut), .clk(clock), .clr(clear));
  Register u_read_data_2 (.D(read_data_2), .en(1'b1), .Q(read_data_2_2), .clk(clock), .clr(clear));
  Register #(.width(4)) u_write_register (
    .D(write_register), .en(1'b1), .Q(write_register_2), .clk(clock), .clr(clear));
endmodule

module MEM_WB (
  input  regwrite,
  input  memtoreg,
  input  [7:0] read_data,
  input  [7:0] aluresult,
  input  [3:0] write_register,
  input  clock,
  input  clear,
  output regwrite_2,
  output memtoreg_2,
  output [7:0] read_data_2,
  output [7:0] aluresukt,
  output [3:0] write_register_2
);

  WB wb_1 (
    .RegWrite(regwrite), .MemToReg(memtoreg), .Clock(clock), .Clear(clear), .RegWrite_2(regwrite_2),
    .MemToReg_2(memtoreg_2));
  Register alu_result (.D(aluresult), .en(1'b1), .Q(aluresukt), .clk(clock), .clr(clear));
  Register u_read_data (.D(read_data), .en(1'b1), .Q(read_data_2), .clk(clock), .clr(clear));
  Register #(.width(4)) u_write_register (
    .D(write_register), .en(1'b1), .Q(write_register_2), .clk(clock), .clr(clear));
endmodule

// stack mem
module stackmemory (
  input  [7:0] Address,
  input  [7:0] Data_Input,
  input  Clear,
  input  sp,
  input  Store,
  input  Clock,
  input  Load,
  input  Chip_Select,
  output [7:0] Data_Loaded
);

  wire and_1_out, and_2_out;

  and and_1 (and_1_out, sp, Store);
  and and_2 (and_2_out, sp, Load);
  RAM #(.bus("separate")) ram_1 (
    .addr(Address), .din(Data_Input), .data(Data_Loaded), .str(and_1_out), .sel(Chip_Select), .clk(Clock),
    .ld(and_2_out), .clr(Clear));
endmodule
