// Logisim project C1_Group1_PIP_LUD.circ as structural Verilog: 2 circuits, main circuit main
module main (
  input  clear,
  output [7:0] alures,
  output [7:0] alures_2,
  output [7:0] read_data_from_mem,
  output [7:0] from_dm,
  output [7:0] PC,
  output [7:0] alures_3,
  output [3:0] rs,
  output [7:0] data,
  output [3:0] rt,
  output [3:0] rd,
  output [7:0] alures_4,
  output [7:0] alures_5,
  output [3:0] shamt,
  output [7:0] A,
  output [7:0] B,
  output [7:0] alures_6,
  output [7:0] write_data,
  output [1:0] forward_A,
  output [3:0] write_reg,
  output [1:0] forward_B,
  output [7:0] zero,
  output [7:0] t0,
  output [7:0] t1,
  output [7:0] t2,
  output [7:0] t3,
  output [7:0] t4,
  output [7:0] t5,
  output [7:0] sp
);

  wire alu_8_by_art_1_p4, and_1_out, and_2_out, and_3_out, clock_out, controlunit_1_alusrc,
       controlunit_1_beq, controlunit_1_bneq, controlunit_1_jump, controlunit_1_memread,
       controlunit_1_memtoreg, controlunit_1_memwrite, controlunit_1_regdst, controlunit_1_regwrite,
       controlunit_1_shift, ex_mem_1_beq_2, ex_mem_1_bneq_2, ex_mem_1_issp_2, ex_mem_1_memread_2,
       ex_mem_1_memtoreg_2, ex_mem_1_memwrite_2, ex_mem_1_zero_2, forwarding_unit_1_p5, forwarding_unit_1_p6,
       id_ex_pip_1_alusrc_2, id_ex_pip_1_beq_2, id_ex_pip_1_bneq_2, id_ex_pip_1_issp_2,
       id_ex_pip_1_memread_2, id_ex_pip_1_memtoreg_2, id_ex_pip_1_memwrite_2, id_ex_pip_1_regdst_2,
       id_ex_pip_1_regwrite_2, id_ex_pip_1_shift_2, load_use_detector_1_stall, mem_wb_1_memtoreg_2,
       not_1_out, not_2_out;
  wire [1:0] priority_encoder_1_out;
  wire [2:0] controlunit_1_aluop, id_ex_pip_1_auop;
  wire [3:0] forwarding_unit_1_p1, id_ex_pip_1_rd_2, id_ex_pip_1_rs_2, id_ex_pip_1_rt_2, multiplexer_6_out;
  wire [7:0] adder_1_out, adder_2_out, datamemory_1_data_loaded, ex_mem_1_pc_4_2, ex_mem_1_pc_4_shift_2,
       id_ex_pip_1_pc_4_2, id_ex_pip_1_read_data_1_2, id_ex_pip_1_read_data_2_2, id_ex_pip_1_signed_extended,
       if_id_1_pc_4_2, multiplexer_1_out, multiplexer_3_out, multiplexer_4_out, multiplexer_5_out,
       multiplexer_7_out, register_file_1_read_data_1, register_file_1_read_data_2, stackmemory_1_data_loaded;
  wire [19:0] insruction_memory_1_instruction;
  wire [19:16] if_id_1_instruction_2;

  Priority_Encoder #(.select(2)) priority_encoder_1 (
    .in0(1'b1), .in1(and_2_out), .in2(and_3_out), .in3(controlunit_1_jump), .out(priority_encoder_1_out));  // open: gs, en_out, en_in
  Multiplexer #(.select(2), .width(8), .enable("false")) multiplexer_1 (
    .in0(adder_1_out), .in1(ex_mem_1_pc_4_shift_2), .in2(ex_mem_1_pc_4_shift_2), .in3({rs, rd}),
    .out(multiplexer_1_out), .sel(priority_encoder_1_out));
  Clock clock (.out(clock_out));
  Register #(.trigger("falling")) PC_reg (.D(multiplexer_1_out), .Q(PC), .clk(clock_out), .clr(clear));  // open: en
  Adder adder_1 (.a(PC), .b(8'h1), .out(adder_1_out));  // open: cin, cout
  Insruction_memory insruction_memory_1 (.PC(PC), .Instruction(insruction_memory_1_instruction));
  IF_ID if_id_1 (
    .pc_4(adder_1_out), .Instruction(insruction_memory_1_instruction), .Clock(clock_out), .Clear(clear),
    .pc_4_2(if_id_1_pc_4_2), .Instruction_2({if_id_1_instruction_2, rs, rd, shamt, alures_6[3:0]}));
  ControlUnit controlunit_1 (
    .PC(if_id_1_instruction_2), .AluOp(controlunit_1_aluop), .AluSrc(controlunit_1_alusrc),
    .bneq(controlunit_1_bneq), .beq(controlunit_1_beq), .memToReg(controlunit_1_memtoreg),
    .memWrite(controlunit_1_memwrite), .memRead(controlunit_1_memread), .RegWrite(controlunit_1_regwrite),
    .RegDst(controlunit_1_regdst), .shift(controlunit_1_shift), .jump(controlunit_1_jump));
  Multiplexer #(.width(4), .enable("false")) multiplexer_2 (
    .in0(shamt), .in1(4'b0000), .out(alures_6[7:4]), .sel(controlunit_1_shift));
  not not_1 (not_1_out, rs[3]);
  load_use_detector load_use_detector_1 (
    .IF_ID_Rs(rs), .IF_ID_Rt(rd), .ID_EX_Rt(id_ex_pip_1_rt_2), .ID_EX_MemRead(id_ex_pip_1_memread_2),
    .Stall(load_use_detector_1_stall));
  and and_1 (and_1_out, rs[0], rs[1], rs[2], not_1_out);
  Register_File register_file_1 (
    .Read_Reg1__rs(rs), .Read_Reg2__rt(rd), .Write_register(write_reg), .Write_Data(alures_4),
    .Write_signal(forwarding_unit_1_p5), .Clock(clock_out), .clear(clear),
    .Read_data_1(register_file_1_read_data_1), .Read_data_2(register_file_1_read_data_2), .zero(zero),
    .t0(t0), .t1(t1), .t2(t2), .t3(t3), .t4(t4), .t5(t5), .sp(sp));
  ID_EX_PIP id_ex_pip_1 (
    .Stall(load_use_detector_1_stall), .isSP(and_1_out), .regwrite(controlunit_1_regwrite),
    .memtoreg(controlunit_1_memtoreg), .beq(controlunit_1_beq), .bneq(controlunit_1_bneq),
    .memread(controlunit_1_memread), .memwrite(controlunit_1_memwrite), .regdst(controlunit_1_regdst),
    .Aluop(controlunit_1_aluop), .Alusrc(controlunit_1_alusrc), .pc_4(multiplexer_3_out),
    .Read_data_1(register_file_1_read_data_1), .Read_data_2(register_file_1_read_data_2),
    .sign_extended(alures_6), .rt(rd), .rd(shamt), .rs(rs), .shift(controlunit_1_shift), .clock(clock_out),
    .clear(clear), .isSp_2(id_ex_pip_1_issp_2), .regwrite_2(id_ex_pip_1_regwrite_2),
    .memtoreg_2(id_ex_pip_1_memtoreg_2), .beq_2(id_ex_pip_1_beq_2), .bneq_2(id_ex_pip_1_bneq_2),
    .memread_2(id_ex_pip_1_memread_2), .memwrite_2(id_ex_pip_1_memwrite_2), .regdst_2(id_ex_pip_1_regdst_2),
    .Auop(id_ex_pip_1_auop), .alusrc_2(id_ex_pip_1_alusrc_2), .pc_4_2(id_ex_pip_1_pc_4_2),
    .read_data_1_2(id_ex_pip_1_read_data_1_2), .read_data_2_2(id_ex_pip_1_read_data_2_2),
    .signed_extended(id_ex_pip_1_signed_extended), .rt_2(id_ex_pip_1_rt_2), .rd_2(id_ex_pip_1_rd_2),
    .rs_2(id_ex_pip_1_rs_2), .shift_2(id_ex_pip_1_shift_2));  // open: Not_Needed
  Multiplexer #(.width(8), .enable("false")) multiplexer_3 (
    .in0(if_id_1_pc_4_2), .in1(PC), .out(multiplexer_3_out), .sel(load_use_detector_1_stall));
  Multiplexer #(.width(8), .enable("false")) multiplexer_4 (
    .in0(id_ex_pip_1_read_data_1_2), .in1(multiplexer_7_out), .out(multiplexer_4_out),
    .sel(id_ex_pip_1_shift_2));
  Multiplexer #(.width(8), .enable("false")) multiplexer_5 (
    .in0(multiplexer_7_out), .in1(id_ex_pip_1_read_data_1_2), .out(multiplexer_5_out),
    .sel(id_ex_pip_1_shift_2));
  Multiplexer #(.width(4), .enable("false")) multiplexer_6 (
    .in0(id_ex_pip_1_rt_2), .in1(id_ex_pip_1_rd_2), .out(multiplexer_6_out), .sel(id_ex_pip_1_regdst_2));
  Adder adder_2 (.a(id_ex_pip_1_pc_4_2), .b(id_ex_pip_1_signed_extended), .out(adder_2_out), .cin(1'b0));  // open: cout
  Multiplexer #(.width(8), .enable("false")) multiplexer_7 (
    .in0(id_ex_pip_1_read_data_2_2), .in1(id_ex_pip_1_signed_extended), .out(multiplexer_7_out),
    .sel(id_ex_pip_1_alusrc_2));
  Multiplexer #(.select(2), .width(8), .enable("false")) multiplexer_8 (
    .in0(multiplexer_4_out), .in1(alures_4), .in2(alures), .out(A), .sel(forward_A));  // open: in3
  // Forwarding_Unit forwarding_unit_1: pin names not known; wires that end beside it: forwarding_unit_1_p1, id_ex_pip_1_rs_2, id_ex_pip_1_rt_2, write_reg, forwarding_unit_1_p5, forwarding_unit_1_p6, forward_A, forward_B
  // ALU_8_by_ART alu_8_by_art_1: pin names not known; wires that end beside it: A, B, id_ex_pip_1_auop, alu_8_by_art_1_p4, alures_5
  Multiplexer #(.select(2), .width(8), .enable("false")) multiplexer_9 (
    .in0(multiplexer_5_out), .in1(alures_4), .in2(alures), .out(B), .sel(forward_B));  // open: in3
  EX_MEM ex_mem_1 (
    .isSP(id_ex_pip_1_issp_2), .regwrite(id_ex_pip_1_regwrite_2), .memtoreg(id_ex_pip_1_memtoreg_2),
    .beq(id_ex_pip_1_beq_2), .bneq(id_ex_pip_1_bneq_2), .memread(id_ex_pip_1_memread_2),
    .memwrite(id_ex_pip_1_memwrite_2), .pc_4_shift(adder_2_out), .pc_4(id_ex_pip_1_pc_4_2),
    .zero(alu_8_by_art_1_p4), .alu_result(alures_5), .read_data_2(id_ex_pip_1_read_data_2_2),
    .write_register(multiplexer_6_out), .clock(clock_out), .clear(clear), .isSp_2(ex_mem_1_issp_2),
    .regwrite_2(forwarding_unit_1_p6), .memtoreg_2(ex_mem_1_memtoreg_2), .beq_2(ex_mem_1_beq_2),
    .bneq_2(ex_mem_1_bneq_2), .memread_2(ex_mem_1_memread_2), .memwrite_2(ex_mem_1_memwrite_2),
    .pc_4_shift_2(ex_mem_1_pc_4_shift_2), .pc_4_2(ex_mem_1_pc_4_2), .zero_2(ex_mem_1_zero_2),
    .alureslut(alures), .read_data_2_2(data), .write_register_2(forwarding_unit_1_p1));
  not not_2 (not_2_out, ex_mem_1_zero_2);
  and and_2 (and_2_out, ex_mem_1_bneq_2, not_2_out);
  and and_3 (and_3_out, ex_mem_1_beq_2, ex_mem_1_zero_2);
  dataMemory datamemory_1 (
    .Address(alures), .Data_Input(data), .isSP(ex_mem_1_issp_2), .Store(ex_mem_1_memwrite_2),
    .Clock(clock_out), .Load(ex_mem_1_memread_2), .clear(clear), .Data_Loaded(datamemory_1_data_loaded));  // open: Chip_Select
  stackmemory stackmemory_1 (
    .Address(alures), .Data_Input(data), .sp(ex_mem_1_issp_2), .Store(ex_mem_1_memwrite_2),
    .Clock(clock_out), .Load(ex_mem_1_memread_2), .Clear(clear), .Data_Loaded(stackmemory_1_data_loaded));  // open: Chip_Select
  MEM_WB mem_wb_1 (
    .regwrite(forwarding_unit_1_p6), .memtoreg(ex_mem_1_memtoreg_2), .read_data(read_data_from_mem),
    .aluresult(alures), .write_register(forwarding_unit_1_p1), .clock(clock_out), .clear(clear),
    .regwrite_2(forwarding_unit_1_p5), .memtoreg_2(mem_wb_1_memtoreg_2), .read_data_2(from_dm),
    .aluresukt(alures_2), .write_register_2(write_reg));
  Multiplexer #(.width(8), .enable("false")) multiplexer_10 (
    .in0(datamemory_1_data_loaded), .in1(stackmemory_1_data_loaded), .out(read_data_from_mem),
    .sel(ex_mem_1_issp_2));
  Multiplexer #(.width(8), .enable("false")) multiplexer_11 (
    .in0(alures_2), .in1(from_dm), .out(alures_4), .sel(mem_wb_1_memtoreg_2));

  assign alures_3 = alures;
  assign rt = rd;
  assign write_data = alures_4;
endmodule

module ID_EX_PIP (
  input  Stall,
  input  isSP,
  input  regwrite,
  input  memtoreg,
  input  beq,
  input  bneq,
  input  memread,
  input  memwrite,
  input  regdst,
  input  [2:0] Aluop,
  input  Alusrc,
  input  [7:0] pc_4,
  input  [7:0] Read_data_1,
  input  [7:0] Read_data_2,
  input  [7:0] sign_extended,
  input  [3:0] rt,
  input  [3:0] rd,
  input  [3:0] rs,
  input  shift,
  input  clock,
  input  clear,
  output Not_Needed,
  output isSp_2,
  output regwrite_2,
  output memtoreg_2,
  output beq_2,
  output bneq_2,
  output memread_2,
  output memwrite_2,
  output regdst_2,
  output [2:0] Auop,
  output alusrc_2,
  output [7:0] pc_4_2,
  output [7:0] read_data_1_2,
  output [7:0] read_data_2_2,
  output [7:0] signed_extended,
  output [3:0] rt_2,
  output [3:0] rd_2,
  output [3:0] rs_2,
  output shift_2
);

  wire and_1_out, and_2_out, and_3_out, and_4_out, and_5_out, and_6_out, and_7_out, and_8_out, not_1_out,
       not_2_out, not_3_out, not_4_out, not_5_out, not_6_out, not_7_out, not_8_out;

  not not_1 (not_1_out, Stall);
  not not_2 (not_2_out, Stall);
  not not_3 (not_3_out, Stall);
  not not_4 (not_4_out, Stall);
  not not_5 (not_5_out, Stall);
  not not_6 (not_6_out, Stall);
  not not_7 (not_7_out, Stall);
  not not_8 (not_8_out, Stall);
  and and_1 (and_1_out, not_1_out, regwrite);
  and and_2 (and_2_out, not_2_out, memtoreg);
  and and_3 (and_3_out, not_3_out, beq);
  and and_4 (and_4_out, not_4_out, bneq);
  and and_5 (and_5_out, not_5_out, memread);
  and and_6 (and_6_out, not_6_out, memwrite);
  and and_7 (and_7_out, not_7_out, regdst);
  and and_8 (and_8_out, not_8_out, Alusrc);
  Register #(.width(4)) u_rs (.D(rs), .en(1'b1), .Q(rs_2), .clk(clock), .clr(clear));
  Register #(.width(1)) u_shift (.D(shift), .en(1'b1), .Q(shift_2), .clk(clock), .clr(clear));
  Register #(.width(1)) u_issp (.D(isSP), .en(1'b1), .Q(isSp_2), .clk(clock), .clr(clear));
  WB wb_1 (
    .RegWrite(and_1_out), .MemToReg(and_2_out), .Clock(clock), .Clear(clear), .RegWrite_2(regwrite_2),
    .MemToReg_2(memtoreg_2));
  M m_1 (
    .beq(and_3_out), .bneq(and_4_out), .MemRead(and_5_out), .MemWrite(and_6_out), .Clock(clock),
    .Clear(clear), .beq_2(beq_2), .bneq_2(bneq_2), .MemRead_2(memread_2), .MemWrite_2(memwrite_2));
  EX ex_1 (
    .Regdst(and_7_out), .AluOp(Aluop), .Alusrc(and_8_out), .clock(clock), .clear(clear), .RegDst_2(regdst_2),
    .AluOp_2(Auop), .Alusrc_2(alusrc_2));
  Register PC__4 (.D(pc_4), .en(1'b1), .Q(pc_4_2), .clk(clock), .clr(clear));
  Register u_Read_data_1 (.D(Read_data_1), .en(1'b1), .Q(read_data_1_2), .clk(clock), .clr(clear));
  Register u_Read_data_2 (.D(Read_data_2), .en(1'b1), .Q(read_data_2_2), .clk(clock), .clr(clear));
  Register u_sign_extended (.D(sign_extended), .en(1'b1), .Q(signed_extended), .clk(clock), .clr(clear));
  Register #(.width(4)) u_rt (.D(rt), .en(1'b1), .Q(rt_2), .clk(clock), .clr(clear));
  Register #(.width(4)) u_rd (.D(rd), .en(1'b1), .Q(rd_2), .clk(clock), .clr(clear));

  assign Not_Needed = isSp_2;
endmodule
