// Logisim project load-use-detector.circ as structural Verilog: 1 circuit, main circuit load-use-detector
module load_use_detector (
  input  [3:0] IF_ID_Rs,
  input  [3:0] IF_ID_Rt,
  input  [3:0] ID_EX_Rt,
  input  ID_EX_MemRead,
  output Stall
);

  wire comparator_1_eq, comparator_2_eq, or_1_out;

  Comparator #(.width(4)) comparator_1 (.a(IF_ID_Rs), .b(ID_EX_Rt), .eq(comparator_1_eq));  // open: gt, lt
  Comparator #(.width(4)) comparator_2 (.a(IF_ID_Rt), .b(ID_EX_Rt), .eq(comparator_2_eq));  // open: gt, lt
  or or_1 (or_1_out, comparator_1_eq, comparator_2_eq);
  and and_1 (Stall, or_1_out, ID_EX_MemRead);
endmodule
