// Logisim project fpa.circ as structural Verilog: 19 circuits, main circuit main
// 22_32
module FractionSplitter (
  input  [21:0] _22_bit_significand,
  input  [8:0] Exponent,
  output [31:0] _32_bit_significand
);

  wire not_1_out, zero_checker_1_is_0;

  Zero_Checker zero_checker_1 (.Exponent(Exponent), .is_0(zero_checker_1_is_0));
  not not_1 (not_1_out, zero_checker_1_is_0);
  and and_1 (_32_bit_significand[30], 1'b1, not_1_out);

  assign {_32_bit_significand[31], _32_bit_significand[29:0]} = {1'b0, _22_bit_significand, {8{1'b0}}};
endmodule

// Inp_split
module Input_Splitter (
  input  [31:0] Input,
  output [31:0] _32_bit_significand,
  output [8:0] _9_bit_exponent,
  output Sign_bit
);

  FractionSplitter fractionsplitter_1 (
    ._22_bit_significand(Input[21:0]), .Exponent(Input[30:22]), ._32_bit_significand(_32_bit_significand));

  assign _9_bit_exponent = Input[30:22];
  assign Sign_bit = Input[31];
endmodule

// ExpDif
module Exponent_Difference (
  input  [8:0] Ea,
  input  [8:0] Eb,
  input  Sa,
  input  Sb,
  output Ea_Eb,
  output [8:0] Ea_Eb_2,
  output [8:0] Smaller_exponent,
  output [8:0] Largest_Exponent,
  output smaller_s_sign,
  output larger_s_sign
);

  Comparator #(.width(9), .mode("unsigned")) comparator_1 (.a(Ea), .b(Eb), .gt(Ea_Eb));  // open: eq, lt
  Multiplexer #(.width(9)) multiplexer_1 (.in0(Ea), .in1(Eb), .out(Smaller_exponent), .sel(Ea_Eb), .en(1'b1));
  Multiplexer #(.width(9)) multiplexer_2 (.in0(Eb), .in1(Ea), .out(Largest_Exponent), .sel(Ea_Eb), .en(1'b1));
  Multiplexer multiplexer_3 (.in0(Sa), .in1(Sb), .out(smaller_s_sign), .sel(Ea_Eb), .en(1'b1));
  Multiplexer multiplexer_4 (.in0(Sb), .in1(Sa), .out(larger_s_sign), .sel(Ea_Eb), .en(1'b1));
  Subtractor #(.width(9)) subtractor_1 (.a(Largest_Exponent), .b(Smaller_exponent), .out(Ea_Eb_2));  // open: bin, bout

  // Notes on the sheet:
  //   Ea
  //   largest
  //   Eb
  //   smallest
endmodule

// Inp
module Sample_Input (
  input  [31:0] A,
  input  [31:0] B,
  output [8:0] largeExp_smallExp,
  output [31:0] Larger_fraction,
  output [31:0] Shifted_smaller_fraction,
  output smaller_s_sign,
  output Larger_s_sign,
  output [31:0] Smaller_fraction,
  output [8:0] Largest_Exponent,
  output [8:0] Smaller_Exponent
);

  wire exponent_difference_1_ea_eb, input_splitter_1_sign_bit, input_splitter_2_sign_bit;
  wire [8:0] input_splitter_1__9_bit_exponent, input_splitter_2__9_bit_exponent;
  wire [31:0] input_splitter_1__32_bit_significand, input_splitter_2__32_bit_significand;

  Input_Splitter input_splitter_1 (
    .Input(A), ._32_bit_significand(input_splitter_1__32_bit_significand),
    ._9_bit_exponent(input_splitter_1__9_bit_exponent), .Sign_bit(input_splitter_1_sign_bit));
  Input_Splitter input_splitter_2 (
    .Input(B), ._32_bit_significand(input_splitter_2__32_bit_significand),
    ._9_bit_exponent(input_splitter_2__9_bit_exponent), .Sign_bit(input_splitter_2_sign_bit));
  Exponent_Difference exponent_difference_1 (
    .Ea(input_splitter_1__9_bit_exponent), .Eb(input_splitter_2__9_bit_exponent),
    .Sa(input_splitter_1_sign_bit), .Sb(input_splitter_2_sign_bit), .Ea_Eb(exponent_difference_1_ea_eb),
    .Ea_Eb_2(largeExp_smallExp), .Smaller_exponent(Smaller_Exponent), .Largest_Exponent(Largest_Exponent),
    .smaller_s_sign(smaller_s_sign), .larger_s_sign(Larger_s_sign));
  Multiplexer #(.width(32)) multiplexer_1 (
    .in0(input_splitter_2__32_bit_significand), .in1(input_splitter_1__32_bit_significand),
    .out(Larger_fraction), .sel(exponent_difference_1_ea_eb), .en(1'b1));
  Multiplexer #(.width(32)) multiplexer_2 (
    .in0(input_splitter_1__32_bit_significand), .in1(input_splitter_2__32_bit_significand),
    .out(Smaller_fraction), .sel(exponent_difference_1_ea_eb), .en(1'b1));
  Right_Shifter right_shifter_1 (
    .significand(Smaller_fraction), .Exponenet_Difference(largeExp_smallExp),
    .significand_output(Shifted_smaller_fraction));
endmodule

// RRS
module Random_Right_Shift (
  input  [31:0] Before_right_shift,
  input  [4:0] Shifting_amount,
  output [31:0] After_right_shift
);

  Shifter #(.width(32), .shift("lr")) shifter_1 (
    .in(Before_right_shift), .\dist (Shifting_amount), .out(After_right_shift));
endmodule

// RLS
module Random_Left_Shift (
  input  [31:0] Before_left_shift,
  input  [4:0] Shifting_amount,
  output [31:0] After_left_shift
);

  Shifter #(.width(32)) shifter_1 (.in(Before_left_shift), .\dist (Shifting_amount), .out(After_left_shift));
endmodule

// Rounding
module Rounding_Circuit (
  input  [31:0] Significand,
  output [31:0] Rounded_significand
);

  wire and_1_out, comparator_1_eq, comparator_1_gt, or_1_out;

  Comparator #(.mode("unsigned")) comparator_1 (
    .a(Significand[7:0]), .b(8'h80), .gt(comparator_1_gt), .eq(comparator_1_eq));  // open: lt
  and and_1 (and_1_out, Significand[8], comparator_1_eq);
  or or_1 (or_1_out, and_1_out, comparator_1_gt);
  Adder #(.width(24)) adder_1 (
    .a(Significand[31:8]), .b({24{1'b0}}), .out(Rounded_significand[31:8]), .cin(or_1_out));  // open: cout

  assign Rounded_significand[7:0] = {8{1'b0}};
endmodule

// RS
module Right_Shifter (
  input  [31:0] significand,
  input  [8:0] Exponenet_Difference,
  output [31:0] significand_output
);

  wire or_1_out;
  wire [31:0] random_right_shift_1_after_right_shift;

  Random_Right_Shift random_right_shift_1 (
    .Before_right_shift(significand), .Shifting_amount(Exponenet_Difference[4:0]),
    .After_right_shift(random_right_shift_1_after_right_shift));
  or or_1 (or_1_out, Exponenet_Difference[8], Exponenet_Difference[7], Exponenet_Difference[6], Exponenet_Difference[5]);
  Multiplexer #(.width(32)) multiplexer_1 (
    .in0(random_right_shift_1_after_right_shift), .in1({32{1'b0}}), .out(significand_output), .sel(or_1_out),
    .en(1'b1));
endmodule

// LRSN
module Left_Right_Shift_Normalizer (
  input  [31:0] Significand,
  input  [4:0] Shift_amount,
  input  Left_or_right_shift_select,
  output [31:0] Output
);

  wire [31:0] random_left_shift_1_after_left_shift, random_right_shift_1_after_right_shift;

  Random_Left_Shift random_left_shift_1 (
    .Before_left_shift(Significand), .Shifting_amount(Shift_amount),
    .After_left_shift(random_left_shift_1_after_left_shift));
  Random_Right_Shift random_right_shift_1 (
    .Before_right_shift(Significand), .Shifting_amount(Shift_amount),
    .After_right_shift(random_right_shift_1_after_right_shift));
  Multiplexer #(.width(32), .enable("false")) multiplexer_1 (
    .in0(random_left_shift_1_after_left_shift), .in1(random_right_shift_1_after_right_shift), .out(Output),
    .sel(Left_or_right_shift_select));
endmodule

// Out_comb
module Output_Combinator (
  input  [21:0] Significand,
  input  [8:0] Exponent,
  input  Sign_bit,
  output [31:0] Final_Output
);


  assign Final_Output = {Sign_bit, Exponent, Significand};
endmodule

// is_0
module Zero_Checker (
  input  [8:0] Exponent,
  output is_0
);

  nor nor_1 (is_0, Exponent[0], Exponent[1], Exponent[2], Exponent[3], Exponent[4], Exponent[5], Exponent[6], Exponent[7], Exponent[8]);
endmodule

// is 1
module One_Checker (
  input  [8:0] Exponent,
  output is_1
);

  and and_1 (is_1, Exponent[0], Exponent[1], Exponent[2], Exponent[3], Exponent[4], Exponent[5], Exponent[6], Exponent[7], Exponent[8]);
endmodule

// AorS
module Adder_Subtractor (
  input  [8:0] Exponent,
  input  [4:0] amount,
  input  add_or_sub,
  output Underflow,
  output [8:0] Output_Exponent,
  output Overflow
);

  wire adder_1_cout, not_1_out, one_checker_1_is_1, or_1_out, or_2_out, subtractor_1_bout,
       zero_checker_1_is_0;
  wire [8:0] adder_1_out, subtractor_1_out;

  Subtractor #(.width(9)) subtractor_1 (
    .a(Exponent), .b({4'b0000, amount}), .out(subtractor_1_out), .bin(1'b0), .bout(subtractor_1_bout));
  Adder #(.width(9)) adder_1 (.a(Exponent), .b({4'b0000, amount}), .out(adder_1_out), .cin(1'b0), .cout(adder_1_cout));
  One_Checker one_checker_1 (.Exponent(Output_Exponent), .is_1(one_checker_1_is_1));
  or or_1 (or_1_out, adder_1_cout, one_checker_1_is_1);
  Zero_Checker zero_checker_1 (.Exponent(Output_Exponent), .is_0(zero_checker_1_is_0));
  Multiplexer #(.width(9), .enable("false")) multiplexer_1 (
    .in0(subtractor_1_out), .in1(adder_1_out), .out(Output_Exponent), .sel(add_or_sub));
  and and_1 (Overflow, add_or_sub, or_1_out);
  not not_1 (not_1_out, add_or_sub);
  or or_2 (or_2_out, subtractor_1_bout, zero_checker_1_is_0);
  and and_2 (Underflow, not_1_out, or_2_out);
endmodule

// Rnorm
module Rounded_Normalizer (
  input  [8:0] Exponent,
  input  [31:0] Significand,
  output [8:0] Normalized_Exponent,
  output Overflow,
  output [31:0] Normalized_Significand,
  output Infinity,
  output Nan
);

  wire adder_1_cout, and_1_out, and_2_out, and_3_out, and_4_out, fractionnonzero_30_1_all_30_bit_0,
       not_1_out, not_2_out, not_3_out, one_checker_1_is_1, one_checker_2_is_1, or_1_out;
  wire [31:0] random_right_shift_1_after_right_shift;

  Random_Right_Shift random_right_shift_1 (
    .Before_right_shift(Significand), .Shifting_amount(5'b00001),
    .After_right_shift(random_right_shift_1_after_right_shift));
  Adder #(.width(9)) adder_1 (
    .a(Exponent), .b({9{1'b0}}), .out(Normalized_Exponent), .cin(Significand[31]), .cout(adder_1_cout));
  Multiplexer #(.width(32), .disabled(0), .enable("false")) multiplexer_1 (
    .in0(Significand), .in1(random_right_shift_1_after_right_shift), .out(Normalized_Significand),
    .sel(Significand[31]));
  One_Checker one_checker_1 (.Exponent(Normalized_Exponent), .is_1(one_checker_1_is_1));
  One_Checker one_checker_2 (.Exponent(Normalized_Exponent), .is_1(one_checker_2_is_1));
  or or_1 (or_1_out, adder_1_cout, one_checker_1_is_1);
  FractionNonzero_30 fractionnonzero_30_1 (
    .Significand(Normalized_Significand[29:0]), .all_30_bit_0(fractionnonzero_30_1_all_30_bit_0));
  and and_1 (and_1_out, or_1_out, Significand[31]);
  not not_1 (not_1_out, fractionnonzero_30_1_all_30_bit_0);
  and and_2 (and_2_out, one_checker_2_is_1, fractionnonzero_30_1_all_30_bit_0);
  and and_3 (and_3_out, one_checker_2_is_1, not_1_out);
  not not_2 (not_2_out, and_2_out);
  not not_3 (not_3_out, and_3_out);
  Multiplexer #(.enable("false")) multiplexer_2 (.in0(1'b0), .in1(and_3_out), .out(Nan), .sel(Significand[31]));
  Multiplexer #(.enable("false")) multiplexer_3 (.in0(1'b0), .in1(and_2_out), .out(Infinity), .sel(Significand[31]));
  and and_4 (and_4_out, and_1_out, not_2_out, not_3_out);
  Multiplexer #(.enable("false")) multiplexer_4 (.in0(1'b0), .in1(and_4_out), .out(Overflow), .sel(Significand[31]));
endmodule

// FPA
module our_fpa (
  input  [31:0] A,
  input  [31:0] B,
  output Underflow,
  output Overflow,
  output [31:0] Output,
  output Denormalised,
  output infinity,
  output Nan,
  output Zero_flag
);

  wire comparator_1_eq, comparator_2_eq, main_1_p6, multiplexer_1_out, normalizer_ckt_1_infinity,
       normalizer_ckt_1_nan, normalizer_ckt_1_overflow, rounded_normalizer_1_infinity,
       rounded_normalizer_1_nan, rounded_normalizer_1_overflow, sample_input_1_larger_s_sign,
       sample_input_1_smaller_s_sign, xor_1_out, zero_checker_1_is_0;
  wire [8:0] normalizer_ckt_1_rounded_exponent, rounded_normalizer_1_normalized_exponent,
       sample_input_1_largest_exponent, sample_input_1_smaller_exponent;
  wire [21:0] rounded_normalizer_1_normalized_significand_2;
  wire [31:0] main_1_p5, normalizer_ckt_1_normalized_significant,
       rounded_normalizer_1_normalized_significand, rounding_circuit_1_rounded_significand,
       sample_input_1_larger_fraction, sample_input_1_shifted_smaller_fraction,
       sample_input_1_smaller_fraction;

  Sample_Input sample_input_1 (
    .A(A), .B(B), .Larger_fraction(sample_input_1_larger_fraction),
    .Shifted_smaller_fraction(sample_input_1_shifted_smaller_fraction),
    .smaller_s_sign(sample_input_1_smaller_s_sign), .Larger_s_sign(sample_input_1_larger_s_sign),
    .Smaller_fraction(sample_input_1_smaller_fraction), .Largest_Exponent(sample_input_1_largest_exponent),
    .Smaller_Exponent(sample_input_1_smaller_exponent));  // open: largeExp_smallExp
  // adder32bit_main main_1: pin names not known; wires that end beside it: sample_input_1_larger_s_sign, sample_input_1_larger_fraction, sample_input_1_shifted_smaller_fraction, sample_input_1_smaller_s_sign, main_1_p5, main_1_p6
  Zero_Checker zero_checker_1 (.Exponent(rounded_normalizer_1_normalized_exponent), .is_0(zero_checker_1_is_0));
  Multiplexer #(.enable("false")) multiplexer_1 (
    .in0(main_1_p6), .in1(1'b0), .out(multiplexer_1_out), .sel(zero_checker_1_is_0));
  Normalizer_ckt normalizer_ckt_1 (
    .Significand(main_1_p5), .Exponent(sample_input_1_largest_exponent),
    .Rounded_Exponent(normalizer_ckt_1_rounded_exponent), .Underflow(Underflow),
    .Overflow(normalizer_ckt_1_overflow), .Normalized_Significant(normalizer_ckt_1_normalized_significant),
    .Denormalised(Denormalised), .Infinity(normalizer_ckt_1_infinity), .Nan(normalizer_ckt_1_nan));
  Comparator #(.width(32), .mode("unsigned")) comparator_1 (
    .a(sample_input_1_larger_fraction), .b(sample_input_1_smaller_fraction), .eq(comparator_1_eq));  // open: gt, lt
  Comparator #(.width(9), .mode("unsigned")) comparator_2 (
    .a(sample_input_1_largest_exponent), .b(sample_input_1_smaller_exponent), .eq(comparator_2_eq));  // open: gt, lt
  xor xor_1 (xor_1_out, sample_input_1_larger_s_sign, sample_input_1_smaller_s_sign);
  Output_Combinator output_combinator_1 (
    .Significand(rounded_normalizer_1_normalized_significand_2),
    .Exponent(rounded_normalizer_1_normalized_exponent), .Sign_bit(multiplexer_1_out), .Final_Output(Output));
  Rounding_Circuit rounding_circuit_1 (
    .Significand(normalizer_ckt_1_normalized_significant),
    .Rounded_significand(rounding_circuit_1_rounded_significand));
  and and_1 (Zero_flag, comparator_1_eq, comparator_2_eq, xor_1_out);
  Rounded_Normalizer rounded_normalizer_1 (
    .Exponent(normalizer_ckt_1_rounded_exponent), .Significand(rounding_circuit_1_rounded_significand),
    .Normalized_Exponent(rounded_normalizer_1_normalized_exponent), .Overflow(rounded_normalizer_1_overflow),
    .Normalized_Significand({rounded_normalizer_1_normalized_significand[31:30], rounded_normalizer_1_normalized_significand_2, rounded_normalizer_1_normalized_significand[7:0]}),
    .Infinity(rounded_normalizer_1_infinity), .Nan(rounded_normalizer_1_nan));
  or or_1 (Overflow, normalizer_ckt_1_overflow, rounded_normalizer_1_overflow);
  or or_2 (infinity, rounded_normalizer_1_infinity, normalizer_ckt_1_infinity);
  or or_3 (Nan, normalizer_ckt_1_nan, rounded_normalizer_1_nan);
endmodule

module main (
  input  [31:0] A,
  input  [31:0] B,
  output Underflow,
  output Overflow,
  output [31:0] Output__Result,
  output Denormalised,
  output Infinity,
  output Nan,
  output zero_flag
);

  our_fpa our_fpa_1 (
    .A(A), .B(B), .Underflow(Underflow), .Overflow(Overflow), .Output(Output__Result),
    .Denormalised(Denormalised), .infinity(Infinity), .Nan(Nan), .Zero_flag(zero_flag));
endmodule

// Frc0chk
module Fraction_nonzero (
  input  [31:0] _32_bit_Significand,
  output all_zero
);

  nor nor_1 (all_zero, _32_bit_Significand[0], _32_bit_Significand[1], _32_bit_Significand[2], _32_bit_Significand[3], _32_bit_Significand[4], _32_bit_Significand[5], _32_bit_Significand[6], _32_bit_Significand[7], _32_bit_Significand[8], _32_bit_Significand[9], _32_bit_Significand[10], _32_bit_Significand[11], _32_bit_Significand[12], _32_bit_Significand[13], _32_bit_Significand[14], _32_bit_Significand[15], _32_bit_Significand[17], _32_bit_Significand[18], _32_bit_Significand[19], _32_bit_Significand[20], _32_bit_Significand[21], _32_bit_Significand[22], _32_bit_Significand[23], _32_bit_Significand[24], _32_bit_Significand[25], _32_bit_Significand[26], _32_bit_Significand[27], _32_bit_Significand[28], _32_bit_Significand[29], _32_bit_Significand[30], _32_bit_Significand[31], _32_bit_Significand[16]);
endmodule

// Frc0chk30
module FractionNonzero_30 (
  input  [29:0] Significand,
  output all_30_bit_0
);

  nor nor_1 (all_30_bit_0, Significand[0], Significand[1], Significand[2], Significand[3], Significand[4], Significand[5], Significand[6], Significand[7], Significand[8], Significand[9], Significand[10], Significand[11], Significand[12], Significand[13], Significand[14], Significand[16], Significand[17], Significand[18], Significand[19], Significand[20], Significand[21], Significand[22], Significand[23], Significand[24], Significand[25], Significand[26], Significand[27], Significand[28], Significand[29], Significand[15]);
endmodule

// NORM
module Normalizer_ckt (
  input  [31:0] Significand,
  input  [8:0] Exponent,
  output [8:0] Rounded_Exponent,
  output Underflow,
  output Overflow,
  output [31:0] Normalized_Significant,
  output Denormalised,
  output Infinity,
  output Nan
);

  wire adder_subtractor_1_overflow, adder_subtractor_1_underflow, and_1_out, and_2_out, and_3_out,
       bitfinder_1_found, fractionnonzero_30_1_all_30_bit_0, fractionnonzero_30_2_all_30_bit_0,
       multiplexer_4_out, multiplexer_5_out, not_1_out, not_2_out, not_3_out, not_4_out, not_5_out,
       not_6_out, not_7_out, not_8_out, not_9_out, one_checker_1_is_1, xor_1_out, zero_checker_1_is_0,
       zero_checker_2_is_0;
  wire [4:0] bitfinder_1_index, multiplexer_1_out, subtractor_1_out;
  wire [8:0] adder_subtractor_1_output_exponent;
  wire [31:0] left_right_shift_normalizer_1_output;

  xor xor_1 (xor_1_out, Significand[31], 1'b1);
  not not_1 (not_1_out, bitfinder_1_found);
  BitFinder #(.width(32), .\type ("high1")) bitfinder_1 (
    .in({1'b0, Significand[30:0]}), .index(bitfinder_1_index), .found(bitfinder_1_found));
  Zero_Checker zero_checker_1 (.Exponent(Exponent), .is_0(zero_checker_1_is_0));
  FractionNonzero_30 fractionnonzero_30_1 (
    .Significand(Significand[29:0]), .all_30_bit_0(fractionnonzero_30_1_all_30_bit_0));
  and and_1 (and_1_out, xor_1_out, not_1_out);
  Subtractor #(.width(5)) subtractor_1 (
    .a(5'b11110), .b(bitfinder_1_index), .out(subtractor_1_out));  // open: bin, bout
  not not_2 (not_2_out, fractionnonzero_30_1_all_30_bit_0);
  Multiplexer #(.width(5), .disabled(0), .enable("false")) multiplexer_1 (
    .in0(subtractor_1_out), .in1(5'b00001), .out(multiplexer_1_out), .sel(Significand[31]));
  Left_Right_Shift_Normalizer left_right_shift_normalizer_1 (
    .Significand(Significand), .Shift_amount(multiplexer_1_out),
    .Left_or_right_shift_select(Significand[31]), .Output(left_right_shift_normalizer_1_output));
  and and_2 (and_2_out, zero_checker_1_is_0, not_2_out);
  Multiplexer #(.width(9), .disabled(0), .enable("false")) multiplexer_2 (
    .in0(adder_subtractor_1_output_exponent), .in1({9{1'b0}}), .out(Rounded_Exponent), .sel(and_1_out));
  Adder_Subtractor adder_subtractor_1 (
    .Exponent(Exponent), .amount(multiplexer_1_out), .add_or_sub(Significand[31]),
    .Underflow(adder_subtractor_1_underflow), .Output_Exponent(adder_subtractor_1_output_exponent),
    .Overflow(adder_subtractor_1_overflow));
  Multiplexer #(.width(32), .disabled(0), .enable("false")) multiplexer_3 (
    .in0(left_right_shift_normalizer_1_output), .in1({32{1'b0}}), .out(Normalized_Significant),
    .sel(and_1_out));
  Multiplexer #(.disabled(0), .enable("false")) multiplexer_4 (
    .in0(adder_subtractor_1_overflow), .in1(1'b0), .out(multiplexer_4_out), .sel(and_1_out));
  not not_3 (not_3_out, and_2_out);
  Multiplexer #(.disabled(0), .enable("false")) multiplexer_5 (
    .in0(adder_subtractor_1_underflow), .in1(1'b0), .out(multiplexer_5_out), .sel(and_1_out));
  not not_4 (not_4_out, multiplexer_4_out);
  Zero_Checker zero_checker_2 (.Exponent(Rounded_Exponent), .is_0(zero_checker_2_is_0));
  FractionNonzero_30 fractionnonzero_30_2 (
    .Significand(Normalized_Significant[29:0]), .all_30_bit_0(fractionnonzero_30_2_all_30_bit_0));
  and and_3 (and_3_out, Normalized_Significant[30], not_4_out, zero_checker_2_is_0);
  not not_5 (not_5_out, Denormalised);
  One_Checker one_checker_1 (.Exponent(Rounded_Exponent), .is_1(one_checker_1_is_1));
  not not_6 (not_6_out, Underflow);
  and and_4 (Underflow, multiplexer_5_out, not_5_out);
  or or_1 (Denormalised, and_3_out, and_2_out);
  not not_7 (not_7_out, fractionnonzero_30_2_all_30_bit_0);
  not not_8 (not_8_out, Infinity);
  not not_9 (not_9_out, Nan);
  and and_5 (Infinity, one_checker_1_is_1, not_6_out, not_3_out, fractionnonzero_30_2_all_30_bit_0);
  and and_6 (Nan, one_checker_1_is_1, not_3_out, not_7_out);
  and and_7 (Overflow, multiplexer_4_out, not_8_out, not_9_out);
endmodule
